// Logisim project JCore1.circ as structural Verilog: 16 circuits, main circuit JC11BAOXN
module JC11BAOXN (
  input  [1:0] OP,
  input  A,
  input  B,
  output O
);

  wire and_1_out, nor_1_out, or_1_out, xor_1_out;

  and and_1 (and_1_out, A, B);
  or or_1 (or_1_out, A, B);
  xor xor_1 (xor_1_out, A, B);
  nor nor_1 (nor_1_out, A, B);
  Multiplexer #(.select(2)) multiplexer_1 (
    .in0(and_1_out), .in1(or_1_out), .in2(xor_1_out), .in3(nor_1_out), .out(O), .sel(OP));
endmodule

module JC18BAOXN (
  input  [7:0] B,
  input  [1:0] Op,
  input  [7:0] A,
  output [7:0] out_4
);

  JC11BAOXN jc11baoxn_1 (.A(A[0]), .B(B[0]), .OP(Op), .O(out_4[0]));
  JC11BAOXN jc11baoxn_2 (.A(A[1]), .B(B[1]), .OP(Op), .O(out_4[1]));
  JC11BAOXN jc11baoxn_3 (.A(A[2]), .B(B[2]), .OP(Op), .O(out_4[2]));
  JC11BAOXN jc11baoxn_4 (.A(A[3]), .B(B[3]), .OP(Op), .O(out_4[3]));
  JC11BAOXN jc11baoxn_5 (.A(A[4]), .B(B[4]), .OP(Op), .O(out_4[4]));
  JC11BAOXN jc11baoxn_6 (.A(A[5]), .B(B[5]), .OP(Op), .O(out_4[5]));
  JC11BAOXN jc11baoxn_7 (.A(A[6]), .B(B[6]), .OP(Op), .O(out_4[6]));
  JC11BAOXN jc11baoxn_8 (.A(A[7]), .B(B[7]), .OP(Op), .O(out_4[7]));
endmodule

module test (
);

  JC164ALU jc164alu_1 ();  // open: A, B, OP, R, CF
endmodule

module JC1FFBAOXN (
  input  [63:0] B,
  input  [1:0] Op,
  input  [63:0] A,
  output [63:0] out_4
);

  JC18BAOXN jc18baoxn_1 (.A(A[7:0]), .B(B[7:0]), .Op(Op), .out_4(out_4[7:0]));
  JC18BAOXN jc18baoxn_2 (.A(A[15:8]), .B(B[15:8]), .Op(Op), .out_4(out_4[15:8]));
  JC18BAOXN jc18baoxn_3 (.A(A[23:16]), .B(B[23:16]), .Op(Op), .out_4(out_4[23:16]));
  JC18BAOXN jc18baoxn_4 (.A(A[31:24]), .B(B[31:24]), .Op(Op), .out_4(out_4[31:24]));
  JC18BAOXN jc18baoxn_5 (.A(A[39:32]), .B(B[39:32]), .Op(Op), .out_4(out_4[39:32]));
  JC18BAOXN jc18baoxn_6 (.A(A[47:40]), .B(B[47:40]), .Op(Op), .out_4(out_4[47:40]));
  JC18BAOXN jc18baoxn_7 (.A(A[55:48]), .B(B[55:48]), .Op(Op), .out_4(out_4[55:48]));
  JC18BAOXN jc18baoxn_8 (.A(A[63:56]), .B(B[63:56]), .Op(Op), .out_4(out_4[63:56]));
endmodule

module JC11BOTP (
  input  DIN,
  input  CLK,
  output DOUT,
  output KOUT
);

  Random #(.seed(2), .width(1)) random_1 (.clr(1'b0), .next(1'b1), .clk(CLK), .out(KOUT));
  JC11BAOXN jc11baoxn_1 (.A(DIN), .B(KOUT), .OP(2'b11), .O(DOUT));
endmodule

module JC11BADD (
  input  A,
  input  B,
  input  Cin,
  output S,
  output Cout
);

  wire and_1_out, and_2_out, xor_1_out;

  xor xor_1 (xor_1_out, A, B);
  and and_1 (and_1_out, Cin, xor_1_out);
  and and_2 (and_2_out, B, A);
  xor xor_2 (S, xor_1_out, Cin);
  or or_1 (Cout, and_1_out, and_2_out);
endmodule

module JC18BADD (
  input  [7:0] A,
  input  [7:0] B,
  input  Cin,
  output [7:0] S,
  output Cout
);

  wire jc11badd_1_cout, jc11badd_2_cout, jc11badd_3_cout, jc11badd_4_cout, jc11badd_5_cout, jc11badd_6_cout,
       jc11badd_7_cout;

  JC11BADD jc11badd_1 (.A(A[0]), .B(B[0]), .Cin(Cin), .S(S[0]), .Cout(jc11badd_1_cout));
  JC11BADD jc11badd_2 (.A(A[1]), .B(B[1]), .Cin(jc11badd_1_cout), .S(S[1]), .Cout(jc11badd_2_cout));
  JC11BADD jc11badd_3 (.A(A[2]), .B(B[2]), .Cin(jc11badd_2_cout), .S(S[2]), .Cout(jc11badd_3_cout));
  JC11BADD jc11badd_4 (.A(A[3]), .B(B[3]), .Cin(jc11badd_3_cout), .S(S[3]), .Cout(jc11badd_4_cout));
  JC11BADD jc11badd_5 (.A(A[4]), .B(B[4]), .Cin(jc11badd_4_cout), .S(S[4]), .Cout(jc11badd_5_cout));
  JC11BADD jc11badd_6 (.A(A[5]), .B(B[5]), .Cin(jc11badd_5_cout), .S(S[5]), .Cout(jc11badd_6_cout));
  JC11BADD jc11badd_7 (.A(A[6]), .B(B[6]), .Cin(jc11badd_6_cout), .S(S[6]), .Cout(jc11badd_7_cout));
  JC11BADD jc11badd_8 (.A(A[7]), .B(B[7]), .Cin(jc11badd_7_cout), .S(S[7]), .Cout(Cout));
endmodule

module JC1FFBADD (
  input  [63:0] A,
  input  [63:0] B,
  input  Cin,
  output [63:0] S,
  output Cout
);

  wire jc18badd_1_cout, jc18badd_2_cout, jc18badd_3_cout, jc18badd_4_cout, jc18badd_5_cout, jc18badd_6_cout,
       jc18badd_7_cout;

  JC18BADD jc18badd_1 (.B(B[7:0]), .Cin(Cin), .A(A[7:0]), .Cout(jc18badd_1_cout), .S(S[7:0]));
  JC18BADD jc18badd_2 (.B(B[15:8]), .Cin(jc18badd_1_cout), .A(A[15:8]), .Cout(jc18badd_2_cout), .S(S[15:8]));
  JC18BADD jc18badd_3 (.B(B[23:16]), .Cin(jc18badd_2_cout), .A(A[23:16]), .Cout(jc18badd_3_cout), .S(S[23:16]));
  JC18BADD jc18badd_4 (.B(B[31:24]), .Cin(jc18badd_3_cout), .A(A[31:24]), .Cout(jc18badd_4_cout), .S(S[31:24]));
  JC18BADD jc18badd_5 (.B(B[39:32]), .Cin(jc18badd_4_cout), .A(A[39:32]), .Cout(jc18badd_5_cout), .S(S[39:32]));
  JC18BADD jc18badd_6 (.B(B[47:40]), .Cin(jc18badd_5_cout), .A(A[47:40]), .Cout(jc18badd_6_cout), .S(S[47:40]));
  JC18BADD jc18badd_7 (.B(B[55:48]), .Cin(jc18badd_6_cout), .A(A[55:48]), .Cout(jc18badd_7_cout), .S(S[55:48]));
  JC18BADD jc18badd_8 (.B(B[63:56]), .Cin(jc18badd_7_cout), .A(A[63:56]), .Cout(Cout), .S(S[63:56]));
endmodule

module JC1LATCH1 (
  input  DI,
  input  WE,
  output DO
);

  wire and_1_out, and_2_out, nor_1_out, not_1_out;

  not not_1 (not_1_out, DI);
  and and_1 (and_1_out, DI, WE);
  and and_2 (and_2_out, not_1_out, WE);
  nor nor_1 (nor_1_out, and_1_out, DO);
  nor nor_2 (DO, nor_1_out, and_2_out);
endmodule

module JC1REG18 (
  input  [7:0] DI,
  input  WE,
  output [7:0] Output_bus_1
);

  JC1LATCH1 JC1LATCH1_1 (.WE(WE), .DI(DI[0]), .DO(Output_bus_1[0]));
  JC1LATCH1 JC1LATCH1_2 (.WE(WE), .DI(DI[1]), .DO(Output_bus_1[1]));
  JC1LATCH1 JC1LATCH1_3 (.WE(WE), .DI(DI[2]), .DO(Output_bus_1[2]));
  JC1LATCH1 JC1LATCH1_4 (.WE(WE), .DI(DI[3]), .DO(Output_bus_1[3]));
  JC1LATCH1 JC1LATCH1_5 (.WE(WE), .DI(DI[4]), .DO(Output_bus_1[4]));
  JC1LATCH1 JC1LATCH1_6 (.WE(WE), .DI(DI[5]), .DO(Output_bus_1[5]));
  JC1LATCH1 JC1LATCH1_7 (.WE(WE), .DI(DI[6]), .DO(Output_bus_1[6]));
  JC1LATCH1 JC1LATCH1_8 (.WE(WE), .DI(DI[7]), .DO(Output_bus_1[7]));
endmodule

module JC1REG164 (
  input  [63:0] DI,
  input  WE,
  output [63:0] DO
);

  JC1REG18 JC1REG18_1 (.WE(WE), .DI(DI[7:0]), .Output_bus_1(DO[7:0]));
  JC1REG18 JC1REG18_2 (.WE(WE), .DI(DI[15:8]), .Output_bus_1(DO[15:8]));
  JC1REG18 JC1REG18_3 (.WE(WE), .DI(DI[23:16]), .Output_bus_1(DO[23:16]));
  JC1REG18 JC1REG18_4 (.WE(WE), .DI(DI[31:24]), .Output_bus_1(DO[31:24]));
  JC1REG18 JC1REG18_5 (.WE(WE), .DI(DI[39:32]), .Output_bus_1(DO[39:32]));
  JC1REG18 JC1REG18_6 (.WE(WE), .DI(DI[47:40]), .Output_bus_1(DO[47:40]));
  JC1REG18 JC1REG18_7 (.WE(WE), .DI(DI[55:48]), .Output_bus_1(DO[55:48]));
  JC1REG18 JC1REG18_8 (.WE(WE), .DI(DI[63:56]), .Output_bus_1(DO[63:56]));
endmodule

module JC1REG1256 (
  input  [63:0] DI0,
  input  [63:0] DI1,
  input  [63:0] DI2,
  input  [63:0] DI3,
  input  WE,
  output [63:0] DO0,
  output [63:0] DO1,
  output [63:0] DO2,
  output [63:0] DO3
);

  JC1REG164 JC1REG164_1 (.WE(WE), .DI(DI0), .DO(DO0));
  JC1REG164 JC1REG164_2 (.WE(WE), .DI(DI1), .DO(DO1));
  JC1REG164 JC1REG164_3 (.WE(WE), .DI(DI2), .DO(DO2));
  JC1REG164 JC1REG164_4 (.WE(WE), .DI(DI3), .DO(DO3));
endmodule

module JC14REG256 (
  input  [1:0] REGID,
  input  WE,
  input  [63:0] DI0,
  input  [63:0] DI1,
  input  [63:0] DI2,
  input  [63:0] DI3,
  output [63:0] DO0,
  output [63:0] DO1,
  output [63:0] DO2,
  output [63:0] DO3
);

  wire and_1_out, and_2_out, and_3_out, and_4_out, decoder_1_out0, decoder_1_out1, decoder_1_out2,
       decoder_1_out3;
  wire [63:0] JC1REG1256_1_do0, JC1REG1256_1_do1, JC1REG1256_1_do2, JC1REG1256_1_do3, JC1REG1256_2_do0,
       JC1REG1256_2_do1, JC1REG1256_2_do2, JC1REG1256_2_do3, JC1REG1256_3_do0, JC1REG1256_3_do1,
       JC1REG1256_3_do2, JC1REG1256_3_do3, JC1REG1256_4_do0, JC1REG1256_4_do1, JC1REG1256_4_do2,
       JC1REG1256_4_do3;

  and and_1 (and_1_out, decoder_1_out0, WE);
  Multiplexer #(.select(2), .width(64)) multiplexer_1 (
    .in0(JC1REG1256_1_do0), .in1(JC1REG1256_3_do0), .in2(JC1REG1256_2_do0), .in3(JC1REG1256_4_do0),
    .out(DO0), .sel(REGID));
  Decoder #(.select(2)) decoder_1 (
    .out0(decoder_1_out0), .out1(decoder_1_out1), .out2(decoder_1_out2), .out3(decoder_1_out3), .sel(REGID));  // open: en
  and and_2 (and_2_out, decoder_1_out1, WE);
  JC1REG1256 JC1REG1256_1 (
    .WE(and_1_out), .DI1(DI1), .DI2(DI2), .DI3(DI3), .DI0(DI0), .DO1(JC1REG1256_1_do1),
    .DO2(JC1REG1256_1_do2), .DO3(JC1REG1256_1_do3), .DO0(JC1REG1256_1_do0));
  JC1REG1256 JC1REG1256_3 (
    .WE(and_2_out), .DI1(DI1), .DI2(DI2), .DI3(DI3), .DI0(DI0), .DO1(JC1REG1256_3_do1),
    .DO2(JC1REG1256_3_do2), .DO3(JC1REG1256_3_do3), .DO0(JC1REG1256_3_do0));
  Multiplexer #(.select(2), .width(64)) multiplexer_2 (
    .in0(JC1REG1256_1_do1), .in1(JC1REG1256_3_do1), .in2(JC1REG1256_2_do1), .in3(JC1REG1256_4_do1),
    .out(DO1), .sel(REGID));
  and and_3 (and_3_out, WE, decoder_1_out2);
  Multiplexer #(.select(2), .width(64)) multiplexer_3 (
    .in0(JC1REG1256_1_do2), .in1(JC1REG1256_3_do2), .in2(JC1REG1256_2_do2), .in3(JC1REG1256_4_do2),
    .out(DO2), .sel(REGID));
  and and_4 (and_4_out, WE, decoder_1_out3);
  Multiplexer #(.select(2), .width(64)) multiplexer_4 (
    .in0(JC1REG1256_1_do3), .in1(JC1REG1256_3_do3), .in2(JC1REG1256_2_do3), .in3(JC1REG1256_4_do3),
    .out(DO3), .sel(REGID));
  JC1REG1256 JC1REG1256_2 (
    .WE(and_3_out), .DI1(DI1), .DI2(DI2), .DI3(DI3), .DI0(DI0), .DO1(JC1REG1256_2_do1),
    .DO2(JC1REG1256_2_do2), .DO3(JC1REG1256_2_do3), .DO0(JC1REG1256_2_do0));
  JC1REG1256 JC1REG1256_4 (
    .WE(and_4_out), .DI1(DI1), .DI2(DI2), .DI3(DI3), .DI0(DI0), .DO1(JC1REG1256_4_do1),
    .DO2(JC1REG1256_4_do2), .DO3(JC1REG1256_4_do3), .DO0(JC1REG1256_4_do0));
endmodule

module JC18REG64 (
  input  RESET,
  input  WE,
  input  [2:0] REGID,
  input  [63:0] DI,
  output [63:0] DO
);

  wire and_1_out, and_2_out, and_3_out, and_4_out, and_5_out, and_6_out, and_7_out, and_8_out, and_9_out,
       decoder_1_out0, decoder_1_out1, decoder_1_out2, decoder_1_out3, decoder_1_out4, decoder_1_out5,
       decoder_1_out6, decoder_1_out7, not_1_out, or_1_out, or_2_out, or_3_out, or_4_out, or_5_out, or_6_out,
       or_7_out, or_8_out;
  wire [63:0] jc1reg164_1_do, jc1reg164_2_do, jc1reg164_3_do, jc1reg164_4_do, jc1reg164_5_do, jc1reg164_6_do,
       jc1reg164_7_do, jc1reg164_8_do, multiplexer_1_out;

  Multiplexer #(.width(64)) multiplexer_1 (.in0(DI), .in1({64{1'b0}}), .out(multiplexer_1_out), .sel(RESET));
  and and_1 (and_1_out, decoder_1_out0, and_8_out);
  or or_1 (or_1_out, and_1_out, RESET);
  JC1REG164 jc1reg164_1 (.WE(or_1_out), .DI(multiplexer_1_out), .DO(jc1reg164_1_do));
  Decoder #(.select(3)) decoder_1 (
    .out0(decoder_1_out0), .out1(decoder_1_out1), .out2(decoder_1_out2), .out3(decoder_1_out3),
    .out4(decoder_1_out4), .out5(decoder_1_out5), .out6(decoder_1_out6), .out7(decoder_1_out7), .sel(REGID),
    .en(1'b1));
  and and_2 (and_2_out, decoder_1_out1, and_8_out);
  and and_3 (and_3_out, decoder_1_out2, and_8_out);
  or or_2 (or_2_out, and_2_out, RESET);
  JC1REG164 jc1reg164_2 (.WE(or_2_out), .DI(multiplexer_1_out), .DO(jc1reg164_2_do));
  and and_4 (and_4_out, decoder_1_out3, and_8_out);
  or or_3 (or_3_out, and_3_out, RESET);
  JC1REG164 jc1reg164_3 (.WE(or_3_out), .DI(multiplexer_1_out), .DO(jc1reg164_3_do));
  and and_5 (and_5_out, decoder_1_out4, and_8_out);
  or or_4 (or_4_out, and_4_out, RESET);
  or or_5 (or_5_out, and_5_out, RESET);
  JC1REG164 jc1reg164_4 (.WE(or_4_out), .DI(multiplexer_1_out), .DO(jc1reg164_4_do));
  Multiplexer #(.select(3), .width(64)) multiplexer_2 (
    .in0(jc1reg164_1_do), .in1(jc1reg164_2_do), .in2(jc1reg164_3_do), .in3(jc1reg164_4_do),
    .in4(jc1reg164_6_do), .in5(jc1reg164_5_do), .in6(jc1reg164_7_do), .in7(jc1reg164_8_do), .out(DO),
    .sel(REGID));
  and and_6 (and_6_out, decoder_1_out5, and_8_out);
  or or_6 (or_6_out, and_6_out, RESET);
  JC1REG164 jc1reg164_5 (.WE(or_6_out), .DI(multiplexer_1_out), .DO(jc1reg164_5_do));
  JC1REG164 jc1reg164_6 (.WE(or_5_out), .DI(multiplexer_1_out), .DO(jc1reg164_6_do));
  and and_7 (and_7_out, decoder_1_out6, and_8_out);
  or or_7 (or_7_out, and_7_out, RESET);
  JC1REG164 jc1reg164_7 (.WE(or_7_out), .DI(multiplexer_1_out), .DO(jc1reg164_7_do));
  not not_1 (not_1_out, RESET);
  and and_8 (and_8_out, not_1_out, WE);
  and and_9 (and_9_out, decoder_1_out7, and_8_out);
  or or_8 (or_8_out, and_9_out, RESET);
  JC1REG164 jc1reg164_8 (.WE(or_8_out), .DI(multiplexer_1_out), .DO(jc1reg164_8_do));
endmodule

module JC11BALU (
  input  [2:0] OP,
  input  A,
  input  B,
  input  CARRY,
  output C,
  output CF
);

  wire and_1_out, decoder_1_out0, decoder_1_out1, jc11badd_1_cout, jc11badd_1_s, nand_1_out, nor_1_out,
       not_1_out, or_1_out, or_2_out, xor_1_out, xor_2_out, xor_3_out, xor_4_out;

  or or_1 (or_1_out, decoder_1_out0, decoder_1_out1);
  Decoder #(.select(3)) decoder_1 (
    .out0(decoder_1_out0), .out1(decoder_1_out1), .sel(OP), .en(1'b1));  // open: out2, out3, out4, out5, out6, out7
  nand nand_1 (nand_1_out, A, B);
  nor nor_1 (nor_1_out, A, B);
  not not_1 (not_1_out, A);
  Multiplexer #(.select(3)) multiplexer_1 (
    .in0(jc11badd_1_s), .in1(jc11badd_1_s), .in2(nor_1_out), .in3(nand_1_out), .in4(not_1_out),
    .in5(and_1_out), .in6(or_2_out), .in7(xor_2_out), .out(C), .sel(OP));
  and and_1 (and_1_out, A, B);
  or or_2 (or_2_out, A, B);
  xor xor_1 (xor_1_out, B, decoder_1_out1);
  xor xor_2 (xor_2_out, A, B);
  xor xor_3 (xor_3_out, jc11badd_1_cout, decoder_1_out1);
  and and_2 (CF, xor_3_out, or_1_out);
  xor xor_4 (xor_4_out, decoder_1_out1, CARRY);
  JC11BADD jc11badd_1 (.A(A), .B(xor_1_out), .Cin(xor_4_out), .S(jc11badd_1_s), .Cout(jc11badd_1_cout));

  // Notes on the sheet:
  //   IS SUB?
  //   INVERT B (SUB)
  //   3.NAND
  //   OPCODES
  //   0. ADD
  //   4. NOT
  //   1. SUB
  //   5. AND
  //   2. NOR
  //   6. OR 
  //   7. XOR
endmodule

module JC164ALU (
  input  [63:0] A,
  input  [63:0] B,
  input  [2:0] OP,
  output CF,
  output [63:0] R
);

  wire jc11balu_1_cf, jc11balu_2_cf, jc11balu_3_cf, jc11balu_4_cf, jc11balu_5_cf, jc11balu_6_cf,
       jc11balu_7_cf, jc11balu_8_cf, jc11balu_9_cf, jc11balu_10_cf, jc11balu_11_cf, jc11balu_12_cf,
       jc11balu_13_cf, jc11balu_14_cf, jc11balu_15_cf, jc11balu_16_cf, jc11balu_17_cf, jc11balu_18_cf,
       jc11balu_19_cf, jc11balu_20_cf, jc11balu_21_cf, jc11balu_22_cf, jc11balu_23_cf, jc11balu_24_cf,
       jc11balu_25_cf, jc11balu_26_cf, jc11balu_27_cf, jc11balu_28_cf, jc11balu_29_cf, jc11balu_30_cf,
       jc11balu_31_cf, jc11balu_32_cf, jc11balu_33_cf, jc11balu_34_cf, jc11balu_35_cf, jc11balu_36_cf,
       jc11balu_37_cf, jc11balu_38_cf, jc11balu_39_cf, jc11balu_40_cf, jc11balu_41_cf, jc11balu_42_cf,
       jc11balu_43_cf, jc11balu_44_cf, jc11balu_45_cf, jc11balu_46_cf, jc11balu_47_cf, jc11balu_48_cf,
       jc11balu_49_cf, jc11balu_50_cf, jc11balu_51_cf, jc11balu_52_cf, jc11balu_53_cf, jc11balu_54_cf,
       jc11balu_55_cf, jc11balu_56_cf, jc11balu_57_cf, jc11balu_58_cf, jc11balu_59_cf, jc11balu_60_cf,
       jc11balu_61_cf, jc11balu_62_cf, jc11balu_63_cf;

  JC11BALU jc11balu_1 (.OP(OP), .A(A[0]), .B(B[0]), .CARRY(1'b0), .C(R[0]), .CF(jc11balu_1_cf));
  JC11BALU jc11balu_2 (.OP(OP), .A(A[1]), .B(B[1]), .CARRY(jc11balu_1_cf), .C(R[1]), .CF(jc11balu_2_cf));
  JC11BALU jc11balu_3 (.OP(OP), .A(A[2]), .B(B[2]), .CARRY(jc11balu_2_cf), .C(R[2]), .CF(jc11balu_3_cf));
  JC11BALU jc11balu_4 (.OP(OP), .A(A[3]), .B(B[3]), .CARRY(jc11balu_3_cf), .C(R[3]), .CF(jc11balu_4_cf));
  JC11BALU jc11balu_5 (.OP(OP), .A(A[4]), .B(B[4]), .CARRY(jc11balu_4_cf), .C(R[4]), .CF(jc11balu_5_cf));
  JC11BALU jc11balu_6 (.OP(OP), .A(A[5]), .B(B[5]), .CARRY(jc11balu_5_cf), .C(R[5]), .CF(jc11balu_6_cf));
  JC11BALU jc11balu_7 (.OP(OP), .A(A[6]), .B(B[6]), .CARRY(jc11balu_6_cf), .C(R[6]), .CF(jc11balu_7_cf));
  JC11BALU jc11balu_8 (.OP(OP), .A(A[7]), .B(B[7]), .CARRY(jc11balu_7_cf), .C(R[7]), .CF(jc11balu_8_cf));
  JC11BALU jc11balu_9 (.OP(OP), .A(A[8]), .B(B[8]), .CARRY(jc11balu_8_cf), .C(R[8]), .CF(jc11balu_9_cf));
  JC11BALU jc11balu_10 (.OP(OP), .A(A[9]), .B(B[9]), .CARRY(jc11balu_9_cf), .C(R[9]), .CF(jc11balu_10_cf));
  JC11BALU jc11balu_11 (.OP(OP), .A(A[10]), .B(B[10]), .CARRY(jc11balu_10_cf), .C(R[10]), .CF(jc11balu_11_cf));
  JC11BALU jc11balu_12 (.OP(OP), .A(A[11]), .B(B[11]), .CARRY(jc11balu_11_cf), .C(R[11]), .CF(jc11balu_12_cf));
  JC11BALU jc11balu_13 (.OP(OP), .A(A[12]), .B(B[12]), .CARRY(jc11balu_12_cf), .C(R[12]), .CF(jc11balu_13_cf));
  JC11BALU jc11balu_14 (.OP(OP), .A(A[13]), .B(B[13]), .CARRY(jc11balu_13_cf), .C(R[13]), .CF(jc11balu_14_cf));
  JC11BALU jc11balu_15 (.OP(OP), .A(A[14]), .B(B[14]), .CARRY(jc11balu_14_cf), .C(R[14]), .CF(jc11balu_15_cf));
  JC11BALU jc11balu_16 (.OP(OP), .A(A[15]), .B(B[15]), .CARRY(jc11balu_15_cf), .C(R[15]), .CF(jc11balu_16_cf));
  JC11BALU jc11balu_17 (.OP(OP), .A(A[16]), .B(B[16]), .CARRY(jc11balu_16_cf), .C(R[16]), .CF(jc11balu_17_cf));
  JC11BALU jc11balu_18 (.OP(OP), .A(A[17]), .B(B[17]), .CARRY(jc11balu_17_cf), .C(R[17]), .CF(jc11balu_18_cf));
  JC11BALU jc11balu_19 (.OP(OP), .A(A[18]), .B(B[18]), .CARRY(jc11balu_18_cf), .C(R[18]), .CF(jc11balu_19_cf));
  JC11BALU jc11balu_20 (.OP(OP), .A(A[19]), .B(B[19]), .CARRY(jc11balu_19_cf), .C(R[19]), .CF(jc11balu_20_cf));
  JC11BALU jc11balu_21 (.OP(OP), .A(A[20]), .B(B[20]), .CARRY(jc11balu_20_cf), .C(R[20]), .CF(jc11balu_21_cf));
  JC11BALU jc11balu_22 (.OP(OP), .A(A[21]), .B(B[21]), .CARRY(jc11balu_21_cf), .C(R[21]), .CF(jc11balu_22_cf));
  JC11BALU jc11balu_23 (.OP(OP), .A(A[22]), .B(B[22]), .CARRY(jc11balu_22_cf), .C(R[22]), .CF(jc11balu_23_cf));
  JC11BALU jc11balu_24 (.OP(OP), .A(A[23]), .B(B[23]), .CARRY(jc11balu_23_cf), .C(R[23]), .CF(jc11balu_24_cf));
  JC11BALU jc11balu_25 (.OP(OP), .A(A[24]), .B(B[24]), .CARRY(jc11balu_24_cf), .C(R[24]), .CF(jc11balu_25_cf));
  JC11BALU jc11balu_26 (.OP(OP), .A(A[25]), .B(B[25]), .CARRY(jc11balu_25_cf), .C(R[25]), .CF(jc11balu_26_cf));
  JC11BALU jc11balu_27 (.OP(OP), .A(A[26]), .B(B[26]), .CARRY(jc11balu_26_cf), .C(R[26]), .CF(jc11balu_27_cf));
  JC11BALU jc11balu_28 (.OP(OP), .A(A[27]), .B(B[27]), .CARRY(jc11balu_27_cf), .C(R[27]), .CF(jc11balu_28_cf));
  JC11BALU jc11balu_29 (.OP(OP), .A(A[28]), .B(B[28]), .CARRY(jc11balu_28_cf), .C(R[28]), .CF(jc11balu_29_cf));
  JC11BALU jc11balu_30 (.OP(OP), .A(A[29]), .B(B[29]), .CARRY(jc11balu_29_cf), .C(R[29]), .CF(jc11balu_30_cf));
  JC11BALU jc11balu_31 (.OP(OP), .A(A[30]), .B(B[30]), .CARRY(jc11balu_30_cf), .C(R[30]), .CF(jc11balu_31_cf));
  JC11BALU jc11balu_32 (.OP(OP), .A(A[31]), .B(B[31]), .CARRY(jc11balu_31_cf), .C(R[31]), .CF(jc11balu_32_cf));
  JC11BALU jc11balu_33 (.OP(OP), .A(A[32]), .B(B[32]), .CARRY(jc11balu_32_cf), .C(R[32]), .CF(jc11balu_33_cf));
  JC11BALU jc11balu_34 (.OP(OP), .A(A[33]), .B(B[33]), .CARRY(jc11balu_33_cf), .C(R[33]), .CF(jc11balu_34_cf));
  JC11BALU jc11balu_35 (.OP(OP), .A(A[34]), .B(B[34]), .CARRY(jc11balu_34_cf), .C(R[34]), .CF(jc11balu_35_cf));
  JC11BALU jc11balu_36 (.OP(OP), .A(A[35]), .B(B[35]), .CARRY(jc11balu_35_cf), .C(R[35]), .CF(jc11balu_36_cf));
  JC11BALU jc11balu_37 (.OP(OP), .A(A[36]), .B(B[36]), .CARRY(jc11balu_36_cf), .C(R[36]), .CF(jc11balu_37_cf));
  JC11BALU jc11balu_38 (.OP(OP), .A(A[37]), .B(B[37]), .CARRY(jc11balu_37_cf), .C(R[37]), .CF(jc11balu_38_cf));
  JC11BALU jc11balu_39 (.OP(OP), .A(A[38]), .B(B[38]), .CARRY(jc11balu_38_cf), .C(R[38]), .CF(jc11balu_39_cf));
  JC11BALU jc11balu_40 (.OP(OP), .A(A[39]), .B(B[39]), .CARRY(jc11balu_39_cf), .C(R[39]), .CF(jc11balu_40_cf));
  JC11BALU jc11balu_41 (.OP(OP), .A(A[40]), .B(B[40]), .CARRY(jc11balu_40_cf), .C(R[40]), .CF(jc11balu_41_cf));
  JC11BALU jc11balu_42 (.OP(OP), .A(A[41]), .B(B[41]), .CARRY(jc11balu_41_cf), .C(R[41]), .CF(jc11balu_42_cf));
  JC11BALU jc11balu_43 (.OP(OP), .A(A[42]), .B(B[42]), .CARRY(jc11balu_42_cf), .C(R[42]), .CF(jc11balu_43_cf));
  JC11BALU jc11balu_44 (.OP(OP), .A(A[43]), .B(B[43]), .CARRY(jc11balu_43_cf), .C(R[43]), .CF(jc11balu_44_cf));
  JC11BALU jc11balu_45 (.OP(OP), .A(A[44]), .B(B[44]), .CARRY(jc11balu_44_cf), .C(R[44]), .CF(jc11balu_45_cf));
  JC11BALU jc11balu_46 (.OP(OP), .A(A[45]), .B(B[45]), .CARRY(jc11balu_45_cf), .C(R[45]), .CF(jc11balu_46_cf));
  JC11BALU jc11balu_47 (.OP(OP), .A(A[46]), .B(B[46]), .CARRY(jc11balu_46_cf), .C(R[46]), .CF(jc11balu_47_cf));
  JC11BALU jc11balu_48 (.OP(OP), .A(A[47]), .B(B[47]), .CARRY(jc11balu_47_cf), .C(R[47]), .CF(jc11balu_48_cf));
  JC11BALU jc11balu_49 (.OP(OP), .A(A[48]), .B(B[48]), .CARRY(jc11balu_48_cf), .C(R[48]), .CF(jc11balu_49_cf));
  JC11BALU jc11balu_50 (.OP(OP), .A(A[49]), .B(B[49]), .CARRY(jc11balu_49_cf), .C(R[49]), .CF(jc11balu_50_cf));
  JC11BALU jc11balu_51 (.OP(OP), .A(A[50]), .B(B[50]), .CARRY(jc11balu_50_cf), .C(R[50]), .CF(jc11balu_51_cf));
  JC11BALU jc11balu_52 (.OP(OP), .A(A[51]), .B(B[51]), .CARRY(jc11balu_51_cf), .C(R[51]), .CF(jc11balu_52_cf));
  JC11BALU jc11balu_53 (.OP(OP), .A(A[52]), .B(B[52]), .CARRY(jc11balu_52_cf), .C(R[52]), .CF(jc11balu_53_cf));
  JC11BALU jc11balu_54 (.OP(OP), .A(A[53]), .B(B[53]), .CARRY(jc11balu_53_cf), .C(R[53]), .CF(jc11balu_54_cf));
  JC11BALU jc11balu_55 (.OP(OP), .A(A[54]), .B(B[54]), .CARRY(jc11balu_54_cf), .C(R[54]), .CF(jc11balu_55_cf));
  JC11BALU jc11balu_56 (.OP(OP), .A(A[55]), .B(B[55]), .CARRY(jc11balu_55_cf), .C(R[55]), .CF(jc11balu_56_cf));
  JC11BALU jc11balu_57 (.OP(OP), .A(A[56]), .B(B[56]), .CARRY(jc11balu_56_cf), .C(R[56]), .CF(jc11balu_57_cf));
  JC11BALU jc11balu_58 (.OP(OP), .A(A[57]), .B(B[57]), .CARRY(jc11balu_57_cf), .C(R[57]), .CF(jc11balu_58_cf));
  JC11BALU jc11balu_59 (.OP(OP), .A(A[58]), .B(B[58]), .CARRY(jc11balu_58_cf), .C(R[58]), .CF(jc11balu_59_cf));
  JC11BALU jc11balu_60 (.OP(OP), .A(A[59]), .B(B[59]), .CARRY(jc11balu_59_cf), .C(R[59]), .CF(jc11balu_60_cf));
  JC11BALU jc11balu_61 (.OP(OP), .A(A[60]), .B(B[60]), .CARRY(jc11balu_60_cf), .C(R[60]), .CF(jc11balu_61_cf));
  JC11BALU jc11balu_62 (.OP(OP), .A(A[61]), .B(B[61]), .CARRY(jc11balu_61_cf), .C(R[61]), .CF(jc11balu_62_cf));
  JC11BALU jc11balu_63 (.OP(OP), .A(A[62]), .B(B[62]), .CARRY(jc11balu_62_cf), .C(R[62]), .CF(jc11balu_63_cf));
  JC11BALU jc11balu_64 (.OP(OP), .A(A[63]), .B(B[63]), .CARRY(jc11balu_63_cf), .C(R[63]), .CF(CF));
endmodule
